# Fritzing sketch schematic (saved by Fritzing 0.9.4)
breadboards: 1

parts:
  Part1 = Arduino Uno (Rev3) - ICSP
  LCD1 = LCD screen
  S1 = Pushbutton [package="[SMD]"]
  R1 = Resistor [tolerance=±5% resistance=220 package="2010 [SMD]"]
  R2 = Resistor [tolerance=±5% resistance=12k package="0805 [SMD]"]

nets:
  N1: Part1.D11_PWM/MOSI, LCD1.E
  N2: Part1.D12/MISO, LCD1.R/W
  GND: Part1.GND, LCD1.VSS, LCD1.RS, LCD1.LED-, R2.Pin_1
  N3: Part1.D2, LCD1.DB7
  N4: Part1.D3_PWM, LCD1.DB6
  N5: Part1.D4, LCD1.DB5
  N6: Part1.D5_PWM, LCD1.DB4
  N7: Part1.D6_PWM, LCD1.V0
  N8: Part1.D7, S1.Pin_1, S1.Pin_2, R2.Pin_0
  5V: Part1.5V, LCD1.VDD, S1.Pin_3, S1.Pin_4, R1.Pin_1
  N9: LCD1.LED+, R1.Pin_0
